// Logisim project P0.L0.Q1.circ as structural Verilog: 3 circuits, main circuit 4bit_mod
module _4bit_mod (
  input  [3:0] \被除数 ,
  input  [3:0] \除数 ,
  output [2:0] \余数 
);

  wire [3:0] xor_1_out;
  wire [3:3] multiplexer_1_out;

  assign xor_1_out = \被除数  ^ \除数 ;  // XOR_Gate xor_1, 4 bits wide
  Multiplexer #(.width(4)) multiplexer_1 (
    .in0(\被除数 ), .in1(xor_1_out), .out({multiplexer_1_out[3], \余数 }), .sel(\被除数 [3]));  // open: en
endmodule

module CRC (
  input  [7:0] \原数据帧 ,
  input  [3:0] \_4位除数 ,
  output [10:0] \原数据帧_3位校验码 
);

  wire [2:0] \n4bit_mod_1_余数 , \n4bit_mod_2_余数 , \n4bit_mod_3_余数 , \n4bit_mod_4_余数 , \n4bit_mod_5_余数 ,
       \n4bit_mod_6_余数 , \n4bit_mod_7_余数 ;

  _4bit_mod u_4bit_mod_1 (.\被除数 (\原数据帧 [7:4]), .\除数 (\_4位除数 ), .\余数 (\n4bit_mod_1_余数 ));
  _4bit_mod u_4bit_mod_2 (.\被除数 ({\n4bit_mod_1_余数 , \原数据帧 [3]}), .\除数 (\_4位除数 ), .\余数 (\n4bit_mod_2_余数 ));
  _4bit_mod u_4bit_mod_3 (.\被除数 ({\n4bit_mod_2_余数 , \原数据帧 [2]}), .\除数 (\_4位除数 ), .\余数 (\n4bit_mod_3_余数 ));
  _4bit_mod u_4bit_mod_4 (.\被除数 ({\n4bit_mod_3_余数 , \原数据帧 [1]}), .\除数 (\_4位除数 ), .\余数 (\n4bit_mod_4_余数 ));
  _4bit_mod u_4bit_mod_5 (.\被除数 ({\n4bit_mod_4_余数 , \原数据帧 [0]}), .\除数 (\_4位除数 ), .\余数 (\n4bit_mod_5_余数 ));
  _4bit_mod u_4bit_mod_6 (.\被除数 ({\n4bit_mod_5_余数 , 1'b0}), .\除数 (\_4位除数 ), .\余数 (\n4bit_mod_6_余数 ));
  _4bit_mod u_4bit_mod_7 (.\被除数 ({\n4bit_mod_6_余数 , 1'b0}), .\除数 (\_4位除数 ), .\余数 (\n4bit_mod_7_余数 ));
  _4bit_mod u_4bit_mod_8 (.\被除数 ({\n4bit_mod_7_余数 , 1'b0}), .\除数 (\_4位除数 ), .\余数 (\原数据帧_3位校验码 [2:0]));

  assign \原数据帧_3位校验码 [10:3] = \原数据帧 ;
endmodule

module test (
  output [7:0] out_1,
  output [3:0] out_2,
  output [10:0] out_3,
  output out_4
);

  wire clock_1_out;
  wire [7:0] counter_1_q;

  Counter counter_1 (.Q(counter_1_q), .carry(out_4), .clk(clock_1_out));  // open: load, D, count, clr
  Clock clock_1 (.out(clock_1_out));
  ROM #(.dataWidth(12)) rom_1 (.addr(counter_1_q), .data({out_2, out_1}));  // open: sel
  CRC crc_1 (.\原数据帧 (out_1), .\_4位除数 (out_2), .\原数据帧_3位校验码 (out_3));

  // Notes on the sheet:
  //   contents of rom_1 (hex, n*v repeats v):
  //   11f
endmodule
