// Logisim project P0.L0.Q4.circ as structural Verilog: 1 circuit, main circuit fsm
module fsm (
  input  clr,
  input  [1:0] In_1_0,
  output out_3
);

  wire and_1_out, and_2_out, and_3_out, and_4_out, clock_1_out, not_1_out, not_2_out, not_3_out, not_4_out,
       not_5_out, not_6_out, not_7_out, not_8_out, not_9_out;
  wire [1:0] multiplexer_1_out, or_2_out, register_1_q;

  Multiplexer #(.width(2)) multiplexer_1 (.in0(or_2_out), .in1(2'b00), .out(multiplexer_1_out), .sel(clr));  // open: en
  // Probe on multiplexer_1_out
  Clock clock_1 (.out(clock_1_out));
  // Probe on register_1_q
  Register #(.width(2)) register_1 (.D(multiplexer_1_out), .Q(register_1_q), .clk(clock_1_out));  // open: en, clr
  not not_1 (not_1_out, register_1_q[1]);
  not not_2 (not_2_out, In_1_0[0]);
  not not_3 (not_3_out, register_1_q[0]);
  not not_4 (not_4_out, In_1_0[0]);
  not not_5 (not_5_out, In_1_0[1]);
  not not_6 (not_6_out, register_1_q[0]);
  not not_7 (not_7_out, In_1_0[0]);
  not not_8 (not_8_out, register_1_q[0]);
  not not_9 (not_9_out, In_1_0[0]);
  and and_1 (and_1_out, not_1_out, register_1_q[0], not_2_out);
  and and_2 (and_2_out, register_1_q[1], not_3_out, not_4_out);
  and and_3 (and_3_out, not_5_out, In_1_0[0]);
  and and_4 (and_4_out, register_1_q[1], not_6_out, not_7_out);
  and and_5 (out_3, register_1_q[1], not_8_out, not_9_out);
  or or_1 (or_2_out[1], and_1_out, and_2_out);
  or or_2 (or_2_out[0], and_3_out, and_4_out);
  // Probe on or_2_out
endmodule
