// Logisim project p3.circ as structural Verilog: 10 circuits, main circuit IFU
module IFU (
  input  [15:0] imm,
  input  Reset,
  input  [31:0] GPR_rs,
  input  nPC_sel,
  input  zero,
  input  jalr_sel,
  output [31:0] Instr,
  output [31:0] PC_4
);

  wire Clk_out;
  wire [0:0] and_1_out;
  wire [31:0] adder_2_out, bit_extender_1_out, multiplexer_1_out, PC_q, shifter_1_out;

  Adder #(.width(32)) adder_1 (.a(PC_q), .b(32'h4), .out(PC_4));  // open: cin, cout
  assign bit_extender_1_out = {{16{imm[15]}}, imm};  // Bit_Extender bit_extender_1
  Adder #(.width(32)) adder_2 (.a(PC_4), .b(shifter_1_out), .out(adder_2_out));  // open: cin, cout
  Shifter #(.width(32)) shifter_1 (.in(bit_extender_1_out), .\dist (5'b00010), .out(shifter_1_out));
  and and_1 (and_1_out[0], nPC_sel, zero);
  Register #(.width(32)) PC (.D(multiplexer_1_out), .Q(PC_q), .clk(Clk_out), .clr(Reset));  // open: en
  Multiplexer #(.select(2), .width(32)) multiplexer_1 (
    .in0(PC_4), .in1(adder_2_out), .in2(GPR_rs), .out(multiplexer_1_out), .sel({jalr_sel, and_1_out[0]}));  // open: in3, en
  Clock Clk (.out(Clk_out));
  ROM #(.addrWidth(5), .dataWidth(32)) rom_1 (.addr(PC_q[6:2]), .data(Instr));  // open: sel

  // Notes on the sheet:
  //   contents of rom_1 (hex, n*v repeats v):
  //   45484
endmodule

module ALU (
  input  [31:0] A,
  input  [1:0] ALUOp,
  input  [31:0] B,
  output [31:0] C
);

  wire comparator_1_lt;
  wire [31:0] adder_1_out, bit_extender_1_out, or_1_out, subtractor_1_out;

  Adder #(.width(32)) adder_1 (.a(A), .b(B), .out(adder_1_out));  // open: cin, cout
  Subtractor #(.width(32)) subtractor_1 (.a(A), .b(B), .out(subtractor_1_out));  // open: bin, bout
  assign or_1_out = A | B;  // OR_Gate or_1, 32 bits wide
  Comparator #(.width(32)) comparator_1 (.a(A), .b(B), .lt(comparator_1_lt));  // open: gt, eq
  assign bit_extender_1_out = {{31{1'b0}}, comparator_1_lt};  // Bit_Extender bit_extender_1
  Multiplexer #(.select(2), .width(32)) multiplexer_1 (
    .in0(adder_1_out), .in1(subtractor_1_out), .in2(or_1_out), .in3(bit_extender_1_out), .out(C), .sel(ALUOp));  // open: en
endmodule

module DM (
  input  [4:0] Addr,
  input  [31:0] DataIn,
  input  DMwirte,
  input  mem_data,
  input  Reset,
  input  [1:0] sb_byte,
  output [31:0] DataOut
);

  wire Clk_out;
  wire [31:0] multiplexer_1_out, multiplexer_2_out;

  Multiplexer #(.select(2), .width(32)) multiplexer_1 (
    .in0({DataOut[31:8], DataIn[7:0]}), .in1({DataOut[31:16], DataIn[7:0], DataOut[7:0]}),
    .in2({DataOut[31:24], DataIn[7:0], DataOut[15:0]}), .in3({DataIn[7:0], DataOut[23:0]}),
    .out(multiplexer_1_out), .sel(sb_byte));  // open: en
  Multiplexer #(.width(32)) multiplexer_2 (
    .in0(DataIn), .in1(multiplexer_1_out), .out(multiplexer_2_out), .sel(mem_data));  // open: en
  Clock Clk (.out(Clk_out));
  RAM #(.addrWidth(5), .dataWidth(32), .bus("separate")) ram_1 (
    .addr(Addr), .din(multiplexer_2_out), .data(DataOut), .str(DMwirte), .clk(Clk_out), .clr(Reset));  // open: sel, ld
endmodule

module EXT (
  input  [15:0] imm16,
  input  [1:0] EXTOp,
  output [31:0] imm32
);

  wire [31:0] bit_extender_1_out, bit_extender_2_out;

  assign bit_extender_1_out = {{16{1'b0}}, imm16};  // Bit_Extender bit_extender_1
  assign bit_extender_2_out = {{16{imm16[15]}}, imm16};  // Bit_Extender bit_extender_2
  Multiplexer #(.select(2), .width(32)) multiplexer_1 (
    .in0(bit_extender_1_out), .in1(bit_extender_2_out), .in2({imm16, {16{1'b0}}}), .out(imm32), .sel(EXTOp));  // open: in3, en
endmodule

module add_logic (
  input  op5,
  input  op4,
  input  op3,
  input  op2,
  input  op1,
  input  op0,
  input  func5,
  input  func4,
  input  func3,
  input  func2,
  input  func1,
  input  func0,
  output addu,
  output ori,
  output subu,
  output lw,
  output jalr,
  output sw,
  output beq,
  output slt,
  output lui,
  output sb
);

  wire not_1_out, not_2_out, not_3_out, not_4_out, not_5_out, not_6_out, not_7_out, not_8_out, not_9_out,
       not_10_out, not_11_out, not_12_out, Rtype;

  not not_1 (not_1_out, op5);
  not not_2 (not_2_out, op4);
  not not_3 (not_3_out, op3);
  not not_4 (not_4_out, op2);
  not not_5 (not_5_out, op1);
  not not_6 (not_6_out, op0);
  and and_1 (Rtype, not_1_out, not_2_out, not_3_out, not_4_out, not_5_out, not_6_out);
  and and_2 (ori, not_1_out, not_2_out, op3, op2, not_5_out, op0);
  and and_3 (lw, op5, not_2_out, not_3_out, not_4_out, op1, op0);
  and and_4 (sw, op5, not_2_out, op3, not_4_out, op1, op0);
  and and_5 (beq, not_1_out, not_2_out, not_3_out, op2, not_5_out, not_6_out);
  and and_6 (lui, not_1_out, not_2_out, op3, op2, op1, op0);
  and and_7 (sb, op5, not_2_out, op3, not_4_out, not_5_out, not_6_out);
  not not_7 (not_7_out, func5);
  not not_8 (not_8_out, func0);
  not not_9 (not_9_out, func4);
  not not_10 (not_10_out, func3);
  not not_11 (not_11_out, func2);
  not not_12 (not_12_out, func1);
  and and_8 (addu, Rtype, func5, not_9_out, not_10_out, not_11_out, not_12_out, func0);
  and and_9 (subu, Rtype, func5, not_9_out, not_10_out, not_11_out, func1, func0);
  and and_10 (jalr, Rtype, func3, not_7_out, not_9_out, not_11_out, func0, not_12_out);
  and and_11 (slt, Rtype, func5, not_9_out, func3, not_11_out, func1, not_8_out);
endmodule

module or_logic (
  input  addu,
  input  subu,
  input  ori,
  input  lw,
  input  sw,
  input  beq,
  input  lui,
  input  jalr,
  input  sb,
  input  slt,
  output RegDst,
  output ALUSrc,
  output [1:0] MemtoReg,
  output RegWrite,
  output MemWrite,
  output nPC_sel,
  output [1:0] ExtOp,
  output [1:0] ALUctr,
  output jalr_sel,
  output mem_data
);

  or or_1 (MemWrite, sb, sw);
  or or_2 (ExtOp[0], lw, sb, sw);
  or or_3 (ALUctr[0], beq, slt, subu);
  or or_4 (ALUctr[1], slt, ori);
  or or_5 (RegDst, addu, jalr, subu, slt);
  or or_6 (ALUSrc, ori, sb, lw, sw, lui);
  or or_7 (RegWrite, slt, lw, addu, subu, ori, lui, jalr);

  assign ExtOp[1] = lui;
  assign jalr_sel = jalr;
  assign mem_data = sb;
  assign MemtoReg = {jalr, lw};
  assign nPC_sel = beq;
endmodule

module Controller (
  input  [5:0] op,
  input  [5:0] func,
  output RegDst,
  output ALUSrc,
  output [1:0] MemtoReg,
  output RegWrite,
  output MemWrite,
  output nPC_sel,
  output [1:0] ExtOp,
  output [1:0] ALUctr,
  output jalr_esl,
  output mem_data
);

  wire add_logic_1_addu, add_logic_1_beq, add_logic_1_jalr, add_logic_1_lui, add_logic_1_lw, add_logic_1_ori,
       add_logic_1_sb, add_logic_1_slt, add_logic_1_subu, add_logic_1_sw;

  add_logic add_logic_1 (
    .func5(func[5]), .func4(func[4]), .func3(func[3]), .func2(func[2]), .func1(func[1]), .func0(func[0]),
    .addu(add_logic_1_addu), .ori(add_logic_1_ori), .subu(add_logic_1_subu), .lw(add_logic_1_lw),
    .sw(add_logic_1_sw), .beq(add_logic_1_beq), .lui(add_logic_1_lui), .op5(op[5]), .op4(op[4]), .op3(op[3]),
    .op2(op[2]), .op1(op[1]), .op0(op[0]), .jalr(add_logic_1_jalr), .sb(add_logic_1_sb), .slt(add_logic_1_slt));
  or_logic or_logic_1 (
    .addu(add_logic_1_addu), .subu(add_logic_1_subu), .ori(add_logic_1_ori), .lw(add_logic_1_lw),
    .sw(add_logic_1_sw), .beq(add_logic_1_beq), .lui(add_logic_1_lui), .jalr(add_logic_1_jalr),
    .sb(add_logic_1_sb), .RegDst(RegDst), .ALUSrc(ALUSrc), .MemtoReg(MemtoReg), .RegWrite(RegWrite),
    .MemWrite(MemWrite), .nPC_sel(nPC_sel), .ExtOp(ExtOp), .ALUctr(ALUctr), .jalr_sel(jalr_esl),
    .mem_data(mem_data), .slt(add_logic_1_slt));
endmodule

module main (
  input  in_1,
  output [31:0] out_2,
  output out_3,
  output [4:0] out_4,
  output [31:0] out_5,
  output out_6,
  output [4:0] out_7,
  output [31:0] out_8
);

  wire ALUSrc, jalr_sel, mem_data, nPC_sel, RegDst, zero;
  wire [1:0] ALUctr, ExtOp, MemtoReg;
  wire [31:0] alu_1_c, dm_1_dataout, ext_1_imm32, grf_1_rd1, multiplexer_2_out, PC_4;

  Multiplexer #(.width(5)) multiplexer_1 (
    .in0(out_2[20:16]), .in1(out_2[15:11]), .out(out_4), .sel(RegDst));  // open: en
  IFU ifu_1 (
    .imm(out_2[15:0]), .GPR_rs(grf_1_rd1), .nPC_sel(nPC_sel), .zero(zero), .jalr_sel(jalr_sel),
    .Instr(out_2), .Reset(in_1), .PC_4(PC_4));
  GRF grf_1 (
    .A1(out_2[25:21]), .A2(out_2[20:16]), .A3(out_4), .WD(out_5), .Reset(in_1), .WE(out_3), .RD1(grf_1_rd1),
    .RD2(out_8));
  EXT ext_1 (.imm16(out_2[15:0]), .EXTOp(ExtOp), .imm32(ext_1_imm32));
  Multiplexer #(.width(32)) multiplexer_2 (
    .in0(out_8), .in1(ext_1_imm32), .out(multiplexer_2_out), .sel(ALUSrc));  // open: en
  ALU alu_1 (.A(grf_1_rd1), .B(multiplexer_2_out), .ALUOp(ALUctr), .C({alu_1_c[31:7], out_7, alu_1_c[1:0]}));
  Comparator #(.width(32), .mode("unsigned")) comparator_1 (
    .a({32{1'b0}}), .b({alu_1_c[31:7], out_7, alu_1_c[1:0]}), .eq(zero));  // open: gt, lt
  DM dm_1 (
    .Addr(out_7), .DataIn(out_8), .DMwirte(out_6), .DataOut(dm_1_dataout), .Reset(in_1),
    .sb_byte(alu_1_c[1:0]), .mem_data(mem_data));
  Controller Controller (
    .op(out_2[31:26]), .func(out_2[5:0]), .RegDst(RegDst), .ALUSrc(ALUSrc), .MemtoReg(MemtoReg),
    .RegWrite(out_3), .MemWrite(out_6), .nPC_sel(nPC_sel), .ExtOp(ExtOp), .ALUctr(ALUctr),
    .jalr_esl(jalr_sel), .mem_data(mem_data));
  Multiplexer #(.select(2), .width(32)) multiplexer_3 (
    .in0({alu_1_c[31:7], out_7, alu_1_c[1:0]}), .in1(dm_1_dataout), .in2(PC_4), .out(out_5), .sel(MemtoReg));  // open: in3, en

  // Other names for the same wires on the sheet: MemAddr[4:0] = out_7; func[5:0] = out_2[5:0];
  //   imm16[15:0] = out_2[15:0]; Instr[31:0] = out_2; rd[4:0] = out_2[15:11]; rt[4:0] = out_2[20:16];
  //   rs[4:0] = out_2[25:21]; op[5:0] = out_2[31:26]; MemData[31:0] = out_8; MemWrite = out_6; RegAddr[4:0] = out_4;
  //   RegData[31:0] = out_5; RegWrite = out_3; reset = in_1
endmodule

module grf (
  input  [31:0] WD,
  input  [4:0] A3,
  input  WE,
  input  [4:0] A1_A2,
  input  clk,
  input  RESET,
  output [31:0] RD1_RD2
);

  wire decoder_1_out0, decoder_1_out1, decoder_1_out2, decoder_1_out3, decoder_1_out4, decoder_1_out5,
       decoder_1_out6, decoder_1_out7, decoder_1_out8, decoder_1_out9, decoder_1_out10, decoder_1_out11,
       decoder_1_out12, decoder_1_out13, decoder_1_out14, decoder_1_out15, decoder_1_out16, decoder_1_out17,
       decoder_1_out18, decoder_1_out19, decoder_1_out20, decoder_1_out21, decoder_1_out22, decoder_1_out23,
       decoder_1_out24, decoder_1_out25, decoder_1_out26, decoder_1_out27, decoder_1_out28, decoder_1_out29,
       decoder_1_out30, decoder_1_out31;
  wire [31:0] register_1_q, register_2_q, register_3_q, register_4_q, register_5_q, register_6_q,
       register_7_q, register_8_q, register_9_q, register_10_q, register_11_q, register_12_q, register_13_q,
       register_14_q, register_15_q, register_16_q, register_17_q, register_18_q, register_19_q,
       register_20_q, register_21_q, register_22_q, register_23_q, register_24_q, register_25_q,
       register_26_q, register_27_q, register_28_q, register_29_q, register_30_q, register_31_q,
       register_32_q;

  Decoder #(.select(5), .disabled(0)) decoder_1 (
    .out0(decoder_1_out0), .out1(decoder_1_out1), .out2(decoder_1_out2), .out3(decoder_1_out3),
    .out4(decoder_1_out4), .out5(decoder_1_out5), .out6(decoder_1_out6), .out7(decoder_1_out7),
    .out8(decoder_1_out8), .out9(decoder_1_out9), .out10(decoder_1_out10), .out11(decoder_1_out11),
    .out12(decoder_1_out12), .out13(decoder_1_out13), .out14(decoder_1_out14), .out15(decoder_1_out15),
    .out16(decoder_1_out16), .out17(decoder_1_out17), .out18(decoder_1_out18), .out19(decoder_1_out19),
    .out20(decoder_1_out20), .out21(decoder_1_out21), .out22(decoder_1_out22), .out23(decoder_1_out23),
    .out24(decoder_1_out24), .out25(decoder_1_out25), .out26(decoder_1_out26), .out27(decoder_1_out27),
    .out28(decoder_1_out28), .out29(decoder_1_out29), .out30(decoder_1_out30), .out31(decoder_1_out31),
    .sel(A3), .en(WE));
  Register #(.width(32)) register_1 (.D({32{1'b0}}), .en(decoder_1_out0), .Q(register_1_q), .clk(clk), .clr(RESET));
  Register #(.width(32)) register_2 (.D(WD), .en(decoder_1_out4), .Q(register_2_q), .clk(clk), .clr(RESET));
  Register #(.width(32)) register_3 (.D(WD), .en(decoder_1_out8), .Q(register_3_q), .clk(clk), .clr(RESET));
  Register #(.width(32)) register_4 (.D(WD), .en(decoder_1_out12), .Q(register_4_q), .clk(clk), .clr(RESET));
  Register #(.width(32)) register_5 (.D(WD), .en(decoder_1_out16), .Q(register_5_q), .clk(clk), .clr(RESET));
  Register #(.width(32)) register_6 (.D(WD), .en(decoder_1_out20), .Q(register_6_q), .clk(clk), .clr(RESET));
  Register #(.width(32)) register_7 (.D(WD), .en(decoder_1_out24), .Q(register_7_q), .clk(clk), .clr(RESET));
  Register #(.width(32)) register_8 (.D(WD), .en(decoder_1_out28), .Q(register_8_q), .clk(clk), .clr(RESET));
  Register #(.width(32)) register_9 (.D(WD), .en(decoder_1_out29), .Q(register_9_q), .clk(clk), .clr(RESET));
  Register #(.width(32)) register_10 (.D(WD), .en(decoder_1_out1), .Q(register_10_q), .clk(clk), .clr(RESET));
  Register #(.width(32)) register_11 (.D(WD), .en(decoder_1_out5), .Q(register_11_q), .clk(clk), .clr(RESET));
  Register #(.width(32)) register_12 (.D(WD), .en(decoder_1_out9), .Q(register_12_q), .clk(clk), .clr(RESET));
  Register #(.width(32)) register_13 (.D(WD), .en(decoder_1_out13), .Q(register_13_q), .clk(clk), .clr(RESET));
  Register #(.width(32)) register_14 (.D(WD), .en(decoder_1_out17), .Q(register_14_q), .clk(clk), .clr(RESET));
  Register #(.width(32)) register_15 (.D(WD), .en(decoder_1_out21), .Q(register_15_q), .clk(clk), .clr(RESET));
  Register #(.width(32)) register_16 (.D(WD), .en(decoder_1_out25), .Q(register_16_q), .clk(clk), .clr(RESET));
  Register #(.width(32)) register_17 (.D(WD), .en(decoder_1_out2), .Q(register_17_q), .clk(clk), .clr(RESET));
  Register #(.width(32)) register_18 (.D(WD), .en(decoder_1_out6), .Q(register_18_q), .clk(clk), .clr(RESET));
  Register #(.width(32)) register_19 (.D(WD), .en(decoder_1_out10), .Q(register_19_q), .clk(clk), .clr(RESET));
  Register #(.width(32)) register_20 (.D(WD), .en(decoder_1_out14), .Q(register_20_q), .clk(clk), .clr(RESET));
  Register #(.width(32)) register_21 (.D(WD), .en(decoder_1_out18), .Q(register_21_q), .clk(clk), .clr(RESET));
  Register #(.width(32)) register_22 (.D(WD), .en(decoder_1_out22), .Q(register_22_q), .clk(clk), .clr(RESET));
  Register #(.width(32)) register_23 (.D(WD), .en(decoder_1_out26), .Q(register_23_q), .clk(clk), .clr(RESET));
  Register #(.width(32)) register_24 (.D(WD), .en(decoder_1_out30), .Q(register_24_q), .clk(clk), .clr(RESET));
  Register #(.width(32)) register_25 (.D(WD), .en(decoder_1_out3), .Q(register_25_q), .clk(clk), .clr(RESET));
  Register #(.width(32)) register_26 (.D(WD), .en(decoder_1_out7), .Q(register_26_q), .clk(clk), .clr(RESET));
  Register #(.width(32)) register_27 (.D(WD), .en(decoder_1_out11), .Q(register_27_q), .clk(clk), .clr(RESET));
  Register #(.width(32)) register_28 (.D(WD), .en(decoder_1_out15), .Q(register_28_q), .clk(clk), .clr(RESET));
  Register #(.width(32)) register_29 (.D(WD), .en(decoder_1_out19), .Q(register_29_q), .clk(clk), .clr(RESET));
  Register #(.width(32)) register_30 (.D(WD), .en(decoder_1_out23), .Q(register_30_q), .clk(clk), .clr(RESET));
  Register #(.width(32)) register_31 (.D(WD), .en(decoder_1_out27), .Q(register_31_q), .clk(clk), .clr(RESET));
  Register #(.width(32)) register_32 (.D(WD), .en(decoder_1_out31), .Q(register_32_q), .clk(clk), .clr(RESET));
  Multiplexer #(.select(5), .width(32)) multiplexer_1 (
    .in0(register_1_q), .in1(register_10_q), .in2(register_17_q), .in3(register_25_q), .in4(register_2_q),
    .in5(register_11_q), .in6(register_18_q), .in7(register_26_q), .in8(register_3_q), .in9(register_12_q),
    .in10(register_19_q), .in11(register_27_q), .in12(register_4_q), .in13(register_13_q),
    .in14(register_20_q), .in15(register_28_q), .in16(register_5_q), .in17(register_14_q),
    .in18(register_21_q), .in19(register_29_q), .in20(register_6_q), .in21(register_15_q),
    .in22(register_22_q), .in23(register_30_q), .in24(register_7_q), .in25(register_16_q),
    .in26(register_23_q), .in27(register_31_q), .in28(register_8_q), .in29(register_9_q),
    .in30(register_24_q), .in31(register_32_q), .out(RD1_RD2), .sel(A1_A2));  // open: en
endmodule

module GRF (
  input  [4:0] A1,
  input  [4:0] A2,
  input  [4:0] A3,
  input  [31:0] WD,
  input  WE,
  input  Reset,
  output [31:0] RD1,
  output [31:0] RD2
);

  wire Clk_out;

  Clock Clk (.out(Clk_out));
  grf grf_1 (.WD(WD), .A3(A3), .WE(WE), .A1_A2(A1), .clk(Clk_out), .RD1_RD2(RD1), .RESET(Reset));
  grf grf_2 (.WD(WD), .A3(A3), .WE(WE), .A1_A2(A2), .clk(Clk_out), .RD1_RD2(RD2), .RESET(Reset));
endmodule
